// Logisim project 23334046_23378506_Digital Clock_Homework2.circ as structural Verilog: 17 circuits, main circuit UserInterface
module UserInterface (
);

  wire button_1_out, button_2_out, button_3_out, button_4_out, button_5_out, controller_1_alarmmode,
       controller_1_clockmode, controller_1_stopwatchmode, controller_1_timermode, LIGHTS;
  wire [3:0] H1, H10, M1, M10, S1, S10;
  wire [7:0] AMPM;

  Button button_1 (.out(button_1_out));
  Button button_2 (.out(button_2_out));
  Button button_3 (.out(button_3_out));
  Button button_4 (.out(button_4_out));
  Button button_5 (.out(button_5_out));
  Controller controller_1 (
    .Play1224(button_1_out), .DigitReset(button_2_out), .ADD(button_3_out), .StopActivate(button_4_out),
    .MODE(button_5_out), .LIGHTS(LIGHTS), .AMPM(AMPM), .H10(H10), .H1(H1), .M10(M10), .M1(M1), .S10(S10),
    .S1(S1), .ClockMode(controller_1_clockmode), .AlarmMode(controller_1_alarmmode),
    .StopwatchMode(controller_1_stopwatchmode), .TimerMode(controller_1_timermode));  // open: ActiveAlarm
  LED led_1 (.in(controller_1_clockmode));
  LED led_2 (.in(controller_1_alarmmode));
  LED led_3 (.in(controller_1_stopwatchmode));
  LED led_4 (.in(controller_1_timermode));
  // RGBLED rgbled_1: pin names not known
  LED led_5 (.in(LIGHTS));
  LED led_6 (.in(LIGHTS));
  _7_Segment_Display u_7_segment_display_1 ();  // open: g, f, a, b, e, d, c, dp
  // BCD_to_7_Segment_decoder bcd_to_7_segment_decoder_1: pin names not known; wires that end beside it: H10
  LED led_7 (.in(LIGHTS));
  LED led_8 (.in(LIGHTS));
  LED led_9 (.in(LIGHTS));
  LED led_10 (.in(LIGHTS));
  _7_Segment_Display u_7_segment_display_2 ();  // open: g, f, a, b, e, d, c, dp
  // BCD_to_7_Segment_decoder bcd_to_7_segment_decoder_2: pin names not known; wires that end beside it: H1
  LED led_11 (.in(LIGHTS));
  LED led_12 (.in(LIGHTS));
  LED led_13 (.in(LIGHTS));
  LED led_14 (.in(LIGHTS));
  _7_Segment_Display u_7_segment_display_3 ();  // open: g, f, a, b, e, d, c, dp
  // BCD_to_7_Segment_decoder bcd_to_7_segment_decoder_3: pin names not known; wires that end beside it: M10
  LED led_15 (.in(LIGHTS));
  LED led_16 (.in(LIGHTS));
  LED led_17 (.in(LIGHTS));
  LED led_18 (.in(LIGHTS));
  _7_Segment_Display u_7_segment_display_4 ();  // open: g, f, a, b, e, d, c, dp
  // BCD_to_7_Segment_decoder bcd_to_7_segment_decoder_4: pin names not known; wires that end beside it: M1
  LED led_19 (.in(LIGHTS));
  LED led_20 (.in(LIGHTS));
  LED led_21 (.in(LIGHTS));
  LED led_22 (.in(LIGHTS));
  _7_Segment_Display u_7_segment_display_5 ();  // open: g, f, a, b, e, d, c, dp
  // BCD_to_7_Segment_decoder bcd_to_7_segment_decoder_5: pin names not known; wires that end beside it: S10
  LED led_23 (.in(LIGHTS));
  LED led_24 (.in(LIGHTS));
  LED led_25 (.in(LIGHTS));
  LED led_26 (.in(LIGHTS));
  _7_Segment_Display u_7_segment_display_6 ();  // open: g, f, a, b, e, d, c, dp
  // BCD_to_7_Segment_decoder bcd_to_7_segment_decoder_6: pin names not known; wires that end beside it: S1
  _7_Segment_Display u_7_segment_display_7 (
    .g(AMPM[3]), .f(AMPM[2]), .a(AMPM[1]), .b(AMPM[0]), .e(AMPM[4]), .d(AMPM[5]), .c(AMPM[6]), .dp(AMPM[7]));
endmodule

module Controller (
  input  Play1224,
  input  DigitReset,
  input  ADD,
  input  StopActivate,
  input  MODE,
  output LIGHTS,
  output [7:0] AMPM,
  output [3:0] H10,
  output [3:0] H1,
  output [3:0] M10,
  output [3:0] M1,
  output [3:0] S10,
  output [3:0] S1,
  output ClockMode,
  output AlarmMode,
  output StopwatchMode,
  output TimerMode,
  output ActiveAlarm
);

  wire AlarmADD, AlarmDIGIT, ALARMFLASH, ALARMLIGHTS, ALARMTRIGGER, Clock1224, ClockADD, ClockDIGIT,
       demultiplexer_1_out0, demultiplexer_1_out1, demultiplexer_4_out0, demultiplexer_4_out2,
       demultiplexer_4_out3, demultiplexer_5_out1, demultiplexer_5_out3, DisableAlarm, or_3_out, StopFLASH,
       StopwatchPLAY, StopwatchRESET, TimerADD, TimerDIGIT, TIMERFLASH, TIMERLIGHTS, TimerPLAY;
  wire [1:0] modulo4counter_1_output30;
  wire [3:0] AlarmH1, AlarmH10, AlarmM1, AlarmM10, AlarmS1, AlarmS10, ClockH1, ClockH10, ClockM1, ClockM10,
       ClockS1, ClockS10, StopwatchH1, StopwatchH10, StopwatchM1, StopwatchM10, StopwatchS1, StopwatchS10,
       TimerH1, TimerH10, TimerM1, TimerM10, TimerS1, TimerS10;
  wire [7:0] AlarmAMPM, ClockAMPM;

  Demultiplexer #(.select(2)) demultiplexer_1 (
    .out0(demultiplexer_1_out0), .out1(demultiplexer_1_out1), .out2(StopwatchPLAY), .out3(TimerPLAY),
    .in(Play1224), .sel(modulo4counter_1_output30));
  Demultiplexer #(.select(2)) demultiplexer_2 (
    .out0(ClockDIGIT), .out1(AlarmDIGIT), .out2(StopwatchRESET), .out3(TimerDIGIT), .in(DigitReset),
    .sel(modulo4counter_1_output30));
  Demultiplexer #(.select(2)) demultiplexer_3 (
    .out0(ClockADD), .out1(AlarmADD), .out3(TimerADD), .in(ADD), .sel(modulo4counter_1_output30));  // open: out2
  Demultiplexer #(.select(2)) demultiplexer_4 (
    .out0(demultiplexer_4_out0), .out1(DisableAlarm), .out2(demultiplexer_4_out2),
    .out3(demultiplexer_4_out3), .in(StopActivate), .sel(modulo4counter_1_output30));
  or or_1 (Clock1224, demultiplexer_1_out0, demultiplexer_1_out1);
  or or_2 (StopFLASH, demultiplexer_4_out0, demultiplexer_4_out2, demultiplexer_4_out3);
  MODULO4Counter modulo4counter_1 (.ENABLE(MODE), .Output30(modulo4counter_1_output30));  // open: Reset, STOP
  or or_3 (or_3_out, StopFLASH, DisableAlarm);
  AdjustableClock adjustableclock_1 (
    .SET12Hour(Clock1224), .ADDBUTTON(ClockADD), .DIGIT(ClockDIGIT), .AMPM(ClockAMPM), .H10(ClockH10),
    .H1(ClockH1), .M10(ClockM10), .M1(ClockM1), .S10(ClockS10), .S1(ClockS1));
  Alarm alarm_1 (
    .ADDBUTTON(AlarmADD), .DIGIT(AlarmDIGIT), .SET12Hour(Clock1224), .AMPMc(ClockAMPM), .H10c(ClockH10),
    .H1c(ClockH1), .M6c(ClockM10), .M10c(ClockM1), .S6c(ClockS10), .S10c(ClockS1), .ALARMFLASH(ALARMFLASH),
    .AMPMa(AlarmAMPM), .H10a(AlarmH10), .H1a(AlarmH1), .M6a(AlarmM10), .M10a(AlarmM1), .S6a(AlarmS10),
    .S10a(AlarmS1));
  Stopwatch stopwatch_1 (
    .PAUSEPLAY(StopwatchPLAY), .RESET(StopwatchRESET), .H10(StopwatchH10), .H1(StopwatchH1),
    .M10(StopwatchM10), .M1(StopwatchM1), .S10(StopwatchS10), .S1(StopwatchS1));
  Timer timer_1 (
    .ADDBUTTON(TimerADD), .DIGIT(TimerDIGIT), .PAUSEPLAY(TimerPLAY), .TIMERFLASH(TIMERFLASH),
    .HuTIMER(TimerH10), .HLTIMER(TimerH1), .M6TIMER(TimerM10), .M10TIMER(TimerM1), .S6TIMER(TimerS10),
    .S10TIMER(TimerS1));
  Demultiplexer #(.select(2)) demultiplexer_5 (
    .out0(ClockMode), .out1(demultiplexer_5_out1), .out2(StopwatchMode), .out3(demultiplexer_5_out3),
    .in(1'b1), .sel(modulo4counter_1_output30));
  Flash flash_1 (.Buzz(ALARMFLASH), .RESET(or_3_out), .Lights(ALARMTRIGGER));
  Flash flash_2 (.Buzz(TIMERFLASH), .RESET(StopFLASH), .Lights(TIMERLIGHTS));
  T_Flip_Flop t_ff_1 (.T(1'b1), .clk(DisableAlarm), .Q(ActiveAlarm));  // open: Qn, reset, preset
  Multiplexer #(.select(2), .width(8)) multiplexer_1 (
    .in0(ClockAMPM), .in1(AlarmAMPM), .in2({8{1'b0}}), .in3({8{1'b0}}), .out(AMPM),
    .sel(modulo4counter_1_output30));
  Multiplexer #(.select(2), .width(4)) multiplexer_2 (
    .in0(ClockH10), .in1(AlarmH10), .in2(StopwatchH10), .in3(TimerH10), .out(H10),
    .sel(modulo4counter_1_output30));
  Multiplexer #(.select(2), .width(4)) multiplexer_3 (
    .in0(ClockH1), .in1(AlarmH1), .in2(StopwatchH1), .in3(TimerH1), .out(H1), .sel(modulo4counter_1_output30));
  Multiplexer #(.select(2), .width(4)) multiplexer_4 (
    .in0(ClockM10), .in1(AlarmM10), .in2(StopwatchM10), .in3(TimerM10), .out(M10),
    .sel(modulo4counter_1_output30));
  Multiplexer #(.select(2), .width(4)) multiplexer_5 (
    .in0(ClockM1), .in1(AlarmM1), .in2(StopwatchM1), .in3(TimerM1), .out(M1), .sel(modulo4counter_1_output30));
  Multiplexer #(.select(2), .width(4)) multiplexer_6 (
    .in0(ClockS10), .in1(AlarmS10), .in2(StopwatchS10), .in3(TimerS10), .out(S10),
    .sel(modulo4counter_1_output30));
  Multiplexer #(.select(2), .width(4)) multiplexer_7 (
    .in0(ClockS1), .in1(AlarmS1), .in2(StopwatchS1), .in3(TimerS1), .out(S1), .sel(modulo4counter_1_output30));
  and and_1 (ALARMLIGHTS, ActiveAlarm, ALARMTRIGGER);
  xor xor_1 (TimerMode, demultiplexer_5_out3, TIMERLIGHTS);
  or or_4 (LIGHTS, ALARMLIGHTS, TIMERLIGHTS);
  xor xor_2 (AlarmMode, demultiplexer_5_out1, ALARMLIGHTS);

  // Other names for the same wires on the sheet: ALARMACTIVE = ActiveAlarm
endmodule

module AdjustableClock (
  input  SET12Hour,
  input  ADDBUTTON,
  input  DIGIT,
  output [7:0] AMPM,
  output [3:0] H10,
  output [3:0] H1,
  output [3:0] M10,
  output [3:0] M1,
  output [3:0] S10,
  output [3:0] S1
);

  wire clock_1_out, Hour, M6, M10_t, modulo6counter_1_overflow, modulo6counter_2_overflow,
       modulo10counter_1_overflow, modulo10counter_2_overflow, or_1_out, or_2_out, or_3_out, or_4_out,
       or_5_out, S6, S10_t, t_ff_1_q, undriven;
  wire [3:0] hourscounter12_1_d09, hourscounter12_1_d10, hourscounter24_1_om24l, hourscounter24_1_om24u,
       modulo5counter_1_m5o;

  Demultiplexer #(.select(3)) demultiplexer_1 (
    .out0(S10_t), .out1(S6), .out2(M10_t), .out3(M6), .out4(Hour), .in(ADDBUTTON),
    .sel(modulo5counter_1_m5o[2:0]));  // open: out5, out6, out7
  Modulo5Counter modulo5counter_1 (.HIGH(1'b1), .ENABLE(DIGIT), .M5O(modulo5counter_1_m5o));  // open: RESET, OVERFLOW
  T_Flip_Flop #(.trigger("falling")) t_ff_1 (.T(1'b1), .clk(SET12Hour), .Q(t_ff_1_q));  // open: Qn, reset, preset
  Clock clock_1 (.out(clock_1_out));
  or or_1 (or_1_out, Hour, modulo6counter_1_overflow);
  or or_2 (or_2_out, M6, modulo10counter_1_overflow);
  or or_3 (or_3_out, M10_t, modulo6counter_2_overflow);
  or or_4 (or_4_out, S6, modulo10counter_2_overflow);
  or or_5 (or_5_out, S10_t, clock_1_out);
  HoursCounter12 hourscounter12_1 (
    .HIGH(1'b1), .ENABLE(or_1_out), .SET12Hour(t_ff_1_q), .D10(hourscounter12_1_d10),
    .D09(hourscounter12_1_d09), .AMPM(AMPM));  // open: RESET
  HoursCounter24 hourscounter24_1 (
    .HIGH(1'b1), .ENABLE(or_1_out), .OM24U(hourscounter24_1_om24u), .OM24L(hourscounter24_1_om24l));
  Modulo6Counter modulo6counter_1 (
    .HIGH(1'b1), .ENABLE(or_2_out), .OVERFLOW(modulo6counter_1_overflow), .M6O(M10));  // open: RESET
  Modulo10Counter modulo10counter_1 (
    .HIGH(1'b1), .ENABLE(or_3_out), .OVERFLOW(modulo10counter_1_overflow), .OM10(M1));  // open: RESET
  Modulo6Counter modulo6counter_2 (
    .HIGH(1'b1), .ENABLE(or_4_out), .OVERFLOW(modulo6counter_2_overflow), .M6O(S10));  // open: RESET
  Modulo10Counter modulo10counter_2 (
    .HIGH(1'b1), .ENABLE(or_5_out), .RESET(undriven), .OVERFLOW(modulo10counter_2_overflow), .OM10(S1));
  Multiplexer #(.width(4)) multiplexer_1 (
    .in0(hourscounter24_1_om24u), .in1(hourscounter12_1_d10), .out(H10), .sel(t_ff_1_q));
  Multiplexer #(.width(4)) multiplexer_2 (
    .in0(hourscounter24_1_om24l), .in1(hourscounter12_1_d09), .out(H1), .sel(t_ff_1_q));

  // Other names for the same wires on the sheet: ADD = ADDBUTTON
endmodule

module Alarm (
  input  ADDBUTTON,
  input  DIGIT,
  input  SET12Hour,
  input  [7:0] AMPMc,
  input  [3:0] H10c,
  input  [3:0] H1c,
  input  [3:0] M6c,
  input  [3:0] M10c,
  input  [3:0] S6c,
  input  [3:0] S10c,
  output ALARMFLASH,
  output [7:0] AMPMa,
  output [3:0] H10a,
  output [3:0] H1a,
  output [3:0] M6a,
  output [3:0] M10a,
  output [3:0] S6a,
  output [3:0] S10a
);

  wire and_1_out, clock_1_out, comparator_1_eq, comparator_2_eq, comparator_3_eq, comparator_4_eq,
       comparator_5_eq, comparator_6_eq, comparator_7_eq, H, M6, M10, S6, S10, SET12Hour_t;
  wire [3:0] hourscounter12_1_d09, hourscounter12_1_d10, hourscounter24_1_om24l, hourscounter24_1_om24u,
       modulo5counter_1_m5o;

  T_Flip_Flop t_ff_1 (.T(1'b1), .clk(SET12Hour), .Q(SET12Hour_t));  // open: Qn, reset, preset
  Demultiplexer #(.select(3)) demultiplexer_1 (
    .out0(S10), .out1(S6), .out2(M10), .out3(M6), .out4(H), .in(ADDBUTTON), .sel(modulo5counter_1_m5o[2:0]));  // open: out5, out6, out7
  Modulo5Counter modulo5counter_1 (.HIGH(1'b1), .ENABLE(DIGIT), .M5O(modulo5counter_1_m5o));  // open: RESET, OVERFLOW
  HoursCounter12 hourscounter12_1 (
    .HIGH(1'b1), .ENABLE(H), .SET12Hour(SET12Hour_t), .D10(hourscounter12_1_d10), .D09(hourscounter12_1_d09),
    .AMPM(AMPMa));  // open: RESET
  HoursCounter24 hourscounter24_1 (
    .HIGH(1'b1), .ENABLE(H), .OM24U(hourscounter24_1_om24u), .OM24L(hourscounter24_1_om24l));
  Modulo6Counter modulo6counter_1 (.HIGH(1'b1), .ENABLE(M6), .M6O(M6a));  // open: RESET, OVERFLOW
  Modulo10Counter modulo10counter_1 (.HIGH(1'b1), .ENABLE(M10), .OM10(M10a));  // open: RESET, OVERFLOW
  Modulo6Counter modulo6counter_2 (.HIGH(1'b1), .ENABLE(S6), .M6O(S6a));  // open: RESET, OVERFLOW
  Modulo10Counter modulo10counter_2 (.HIGH(1'b1), .ENABLE(S10), .OM10(S10a));  // open: RESET, OVERFLOW
  Multiplexer #(.width(4)) multiplexer_1 (
    .in0(hourscounter24_1_om24u), .in1(hourscounter12_1_d10), .out(H10a), .sel(SET12Hour_t));
  Multiplexer #(.width(4)) multiplexer_2 (
    .in0(hourscounter24_1_om24l), .in1(hourscounter12_1_d09), .out(H1a), .sel(SET12Hour_t));
  Comparator comparator_1 (.a(AMPMa), .b(AMPMc), .eq(comparator_1_eq));  // open: gt, lt
  Comparator #(.width(4)) comparator_2 (.a(H10a), .b(H10c), .eq(comparator_2_eq));  // open: gt, lt
  Comparator #(.width(4)) comparator_3 (.a(H1a), .b(H1c), .eq(comparator_3_eq));  // open: gt, lt
  Comparator #(.width(4)) comparator_4 (.a(M6a), .b(M6c), .eq(comparator_4_eq));  // open: gt, lt
  Comparator #(.width(4)) comparator_5 (.a(M10a), .b(M10c), .eq(comparator_5_eq));  // open: gt, lt
  Comparator #(.width(4)) comparator_6 (.a(S6a), .b(S6c), .eq(comparator_6_eq));  // open: gt, lt
  Comparator #(.width(4)) comparator_7 (.a(S10a), .b(S10c), .eq(comparator_7_eq));  // open: gt, lt
  and and_1 (and_1_out, comparator_1_eq, comparator_2_eq, comparator_3_eq, comparator_4_eq, comparator_5_eq, comparator_6_eq, comparator_7_eq);
  Clock clock_1 (.out(clock_1_out));
  D_Flip_Flop d_ff_1 (.D(and_1_out), .clk(clock_1_out), .Q(ALARMFLASH));  // open: Qn, preset, reset

  // Other names for the same wires on the sheet: ADD = ADDBUTTON

  // Notes on the sheet:
  //   Current time 
endmodule

module Stopwatch (
  input  PAUSEPLAY,
  input  RESET,
  output [3:0] H10,
  output [3:0] H1,
  output [3:0] M10,
  output [3:0] M1,
  output [3:0] S10,
  output [3:0] S1
);

  wire and_1_out, CLK_out, modulo6counter_1_overflow, modulo6counter_2_overflow, modulo10counter_2_overflow,
       modulo10counter_3_overflow, modulo10counter_4_overflow, t_ff_1_q;

  T_Flip_Flop t_ff_1 (.T(1'b1), .clk(PAUSEPLAY), .Q(t_ff_1_q));  // open: Qn, reset, preset
  Clock CLK (.out(CLK_out));
  and and_1 (and_1_out, CLK_out, t_ff_1_q);
  Modulo10Counter modulo10counter_1 (
    .HIGH(1'b1), .ENABLE(modulo10counter_2_overflow), .RESET(RESET), .OM10(H10));  // open: OVERFLOW
  Modulo10Counter modulo10counter_2 (
    .HIGH(1'b1), .ENABLE(modulo6counter_1_overflow), .RESET(RESET), .OVERFLOW(modulo10counter_2_overflow),
    .OM10(H1));
  Modulo6Counter modulo6counter_1 (
    .HIGH(1'b1), .ENABLE(modulo10counter_3_overflow), .RESET(RESET), .OVERFLOW(modulo6counter_1_overflow),
    .M6O(M10));
  Modulo10Counter modulo10counter_3 (
    .HIGH(1'b1), .ENABLE(modulo6counter_2_overflow), .RESET(RESET), .OVERFLOW(modulo10counter_3_overflow),
    .OM10(M1));
  Modulo6Counter modulo6counter_2 (
    .HIGH(1'b1), .ENABLE(modulo10counter_4_overflow), .RESET(RESET), .OVERFLOW(modulo6counter_2_overflow),
    .M6O(S10));
  Modulo10Counter modulo10counter_4 (
    .HIGH(1'b1), .ENABLE(and_1_out), .RESET(RESET), .OVERFLOW(modulo10counter_4_overflow), .OM10(S1));
endmodule

module Timer (
  input  ADDBUTTON,
  input  DIGIT,
  input  PAUSEPLAY,
  output TIMERFLASH,
  output [3:0] HuTIMER,
  output [3:0] HLTIMER,
  output [3:0] M6TIMER,
  output [3:0] M10TIMER,
  output [3:0] S6TIMER,
  output [3:0] S10TIMER
);

  wire and_1_out, clock_1_out, H1, H10, M1, M10, modulo6down_1_overflow, modulo6down_2_overflow,
       modulo10down_2_overflow, modulo10down_3_overflow, modulo10down_4_overflow, nor_1_out, or_1_out,
       or_2_out, S1, S10, t_ff_1_q, t_ff_2_q;
  wire [3:0] modulo6counter_1_m6o, modulo6counter_2_m6o, modulo6counter_3_m6o, modulo10counter_1_om10,
       modulo10counter_2_om10, modulo10counter_3_om10, modulo10counter_4_om10;

  Demultiplexer #(.select(3)) demultiplexer_1 (
    .out0(S1), .out1(S10), .out2(M1), .out3(M10), .out4(H1), .out5(H10), .in(ADDBUTTON),
    .sel(modulo6counter_1_m6o[2:0]));  // open: out6, out7
  Modulo6Counter modulo6counter_1 (.HIGH(1'b1), .ENABLE(DIGIT), .M6O(modulo6counter_1_m6o));  // open: RESET, OVERFLOW
  Modulo10Counter modulo10counter_1 (
    .HIGH(1'b1), .ENABLE(H10), .OM10(modulo10counter_1_om10));  // open: RESET, OVERFLOW
  Modulo10Counter modulo10counter_2 (.HIGH(1'b1), .ENABLE(H1), .OM10(modulo10counter_2_om10));  // open: RESET, OVERFLOW
  Modulo6Counter modulo6counter_2 (.HIGH(1'b1), .ENABLE(M10), .M6O(modulo6counter_2_m6o));  // open: RESET, OVERFLOW
  Modulo10Counter modulo10counter_3 (.HIGH(1'b1), .ENABLE(M1), .OM10(modulo10counter_3_om10));  // open: RESET, OVERFLOW
  Modulo6Counter modulo6counter_3 (.HIGH(1'b1), .ENABLE(S10), .M6O(modulo6counter_3_m6o));  // open: RESET, OVERFLOW
  Modulo10Counter modulo10counter_4 (.HIGH(1'b1), .ENABLE(S1), .OM10(modulo10counter_4_om10));  // open: RESET, OVERFLOW
  T_Flip_Flop t_ff_1 (.Q(t_ff_1_q), .reset(PAUSEPLAY), .preset(or_1_out));  // open: T, clk, Qn
  T_Flip_Flop t_ff_2 (.T(or_2_out), .clk(or_2_out), .Q(t_ff_2_q));  // open: Qn, reset, preset
  or or_1 (or_1_out, ADDBUTTON, TIMERFLASH);
  and and_1 (and_1_out, t_ff_2_q, clock_1_out);
  Clock clock_1 (.out(clock_1_out));
  or or_2 (or_2_out, TIMERFLASH, PAUSEPLAY);
  modulo10down modulo10down_1 (
    .ADD(t_ff_1_q), .SET(modulo10counter_1_om10), .ENABLE(modulo10down_2_overflow), .O10D(HuTIMER));  // open: OVERFLOW
  modulo10down modulo10down_2 (
    .ADD(t_ff_1_q), .SET(modulo10counter_2_om10), .ENABLE(modulo6down_1_overflow),
    .OVERFLOW(modulo10down_2_overflow), .O10D(HLTIMER));
  Modulo6down modulo6down_1 (
    .ADD(t_ff_1_q), .SET(modulo6counter_2_m6o), .ENABLE(modulo10down_3_overflow),
    .OVERFLOW(modulo6down_1_overflow), .O6D(M6TIMER));
  modulo10down modulo10down_3 (
    .ADD(t_ff_1_q), .SET(modulo10counter_3_om10), .ENABLE(modulo6down_2_overflow),
    .OVERFLOW(modulo10down_3_overflow), .O10D(M10TIMER));
  Modulo6down modulo6down_2 (
    .ADD(t_ff_1_q), .SET(modulo6counter_3_m6o), .ENABLE(modulo10down_4_overflow),
    .OVERFLOW(modulo6down_2_overflow), .O6D(S6TIMER));
  modulo10down modulo10down_4 (
    .ADD(t_ff_1_q), .SET(modulo10counter_4_om10), .ENABLE(and_1_out), .OVERFLOW(modulo10down_4_overflow),
    .O10D(S10TIMER));
  nor nor_1 (nor_1_out, HuTIMER[0], HuTIMER[1], HuTIMER[2], HuTIMER[3], HLTIMER[0], HLTIMER[1], HLTIMER[2], HLTIMER[3], M6TIMER[0], M6TIMER[1], M6TIMER[2], M10TIMER[0], M10TIMER[1], M10TIMER[2], M10TIMER[3], S6TIMER[0], S6TIMER[1], S6TIMER[2], S10TIMER[0], S10TIMER[1], S10TIMER[2], S10TIMER[3]);
  and and_2 (TIMERFLASH, nor_1_out, t_ff_2_q);

  // Other names for the same wires on the sheet: ADD = ADDBUTTON; PLAY = PAUSEPLAY

  // Notes on the sheet:
  //   TIMERFLASH
  //   TIMERFLASH
  //   Counting Down
  //   Counting Down
endmodule

module Flash (
  input  Buzz,
  input  RESET,
  output Lights
);

  wire clock_1_out, modulo4counter_1_stop, modulo10counter_1_overflow, or_1_out, t_ff_1_q;

  T_Flip_Flop #(.trigger("falling")) t_ff_1 (.T(1'b1), .clk(Buzz), .Q(t_ff_1_q), .reset(or_1_out));  // open: Qn, preset
  or or_1 (or_1_out, RESET, modulo4counter_1_stop);
  Clock clock_1 (.out(clock_1_out));
  and and_1 (Lights, t_ff_1_q, clock_1_out);
  Modulo10Counter modulo10counter_1 (
    .HIGH(1'b1), .ENABLE(Lights), .RESET(or_1_out), .OVERFLOW(modulo10counter_1_overflow));  // open: OM10
  MODULO4Counter modulo4counter_1 (
    .Reset(or_1_out), .ENABLE(modulo10counter_1_overflow), .STOP(modulo4counter_1_stop));  // open: Output30
endmodule

module Modulo10Counter (
  input  HIGH,
  input  ENABLE,
  input  RESET,
  output OVERFLOW,
  output [3:0] OM10
);

  wire or_1_out;

  or or_1 (or_1_out, RESET, OVERFLOW);
  T_Flip_Flop #(.trigger("falling")) t_ff_1 (
    .T(HIGH), .clk(OM10[2]), .Q(OM10[3]), .reset(or_1_out));  // open: Qn, preset
  T_Flip_Flop #(.trigger("falling")) t_ff_2 (
    .T(HIGH), .clk(OM10[1]), .Q(OM10[2]), .reset(or_1_out));  // open: Qn, preset
  T_Flip_Flop #(.trigger("falling")) t_ff_3 (
    .T(HIGH), .clk(OM10[0]), .Q(OM10[1]), .reset(or_1_out));  // open: Qn, preset
  T_Flip_Flop #(.trigger("falling")) t_ff_4 (
    .T(HIGH), .clk(ENABLE), .Q(OM10[0]), .reset(or_1_out));  // open: Qn, preset
  and and_1 (OVERFLOW, OM10[3], OM10[1]);
endmodule

module Modulo6Counter (
  input  HIGH,
  input  ENABLE,
  input  RESET,
  output OVERFLOW,
  output [3:0] M6O
);

  wire or_1_out;

  or or_1 (or_1_out, RESET, OVERFLOW);
  T_Flip_Flop #(.trigger("falling")) t_ff_1 (.T(HIGH), .clk(M6O[1]), .Q(M6O[2]), .reset(or_1_out));  // open: Qn, preset
  T_Flip_Flop #(.trigger("falling")) t_ff_2 (.T(HIGH), .clk(M6O[0]), .Q(M6O[1]), .reset(or_1_out));  // open: Qn, preset
  T_Flip_Flop #(.trigger("falling")) t_ff_3 (.T(HIGH), .clk(ENABLE), .Q(M6O[0]), .reset(or_1_out));  // open: Qn, preset
  and and_1 (OVERFLOW, M6O[1], M6O[2]);

  assign M6O[3] = 1'b0;
endmodule

module Modulo5Counter (
  input  HIGH,
  input  ENABLE,
  input  RESET,
  output OVERFLOW,
  output [3:0] M5O
);

  wire or_1_out;

  or or_1 (or_1_out, RESET, OVERFLOW);
  T_Flip_Flop #(.trigger("falling")) t_ff_1 (.T(HIGH), .clk(M5O[1]), .Q(M5O[2]), .reset(or_1_out));  // open: Qn, preset
  T_Flip_Flop #(.trigger("falling")) t_ff_2 (.T(HIGH), .clk(M5O[0]), .Q(M5O[1]), .reset(or_1_out));  // open: Qn, preset
  T_Flip_Flop #(.trigger("falling")) t_ff_3 (.T(HIGH), .clk(ENABLE), .Q(M5O[0]), .reset(or_1_out));  // open: Qn, preset
  and and_1 (OVERFLOW, M5O[0], M5O[2]);

  assign M5O[3] = 1'b0;
endmodule

module MODULO4Counter (
  input  Reset,
  input  ENABLE,
  output [1:0] Output30,
  output STOP
);

  J_K_Flip_Flop j_k_ff_1 (
    .J(Output30[0]), .K(Output30[0]), .clk(ENABLE), .Q(Output30[1]), .reset(Reset));  // open: Qn, preset
  J_K_Flip_Flop j_k_ff_2 (.J(1'b1), .K(1'b1), .clk(ENABLE), .Q(Output30[0]), .reset(Reset));  // open: Qn, preset
  and and_1 (STOP, Output30[1], Output30[0]);
endmodule

module Modulo3Counter (
  input  HIGH,
  input  ENABLE,
  input  RESET,
  output OM3H,
  output OM3L
);

  wire and_1_out, or_1_out;

  or or_1 (or_1_out, RESET, and_1_out);
  T_Flip_Flop #(.trigger("falling")) t_ff_1 (.T(HIGH), .clk(OM3L), .Q(OM3H), .reset(or_1_out));  // open: Qn, preset
  T_Flip_Flop #(.trigger("falling")) t_ff_2 (.T(HIGH), .clk(ENABLE), .Q(OM3L), .reset(or_1_out));  // open: Qn, preset
  and and_1 (and_1_out, OM3L, OM3H);
endmodule

module modulo10down (
  input  ADD,
  input  [3:0] SET,
  input  ENABLE,
  output OVERFLOW,
  output [3:0] O10D
);

  wire and_1_out, and_2_out, and_3_out, and_4_out, and_5_out, demultiplexer_1_out0, demultiplexer_1_out1,
       demultiplexer_2_out0, demultiplexer_2_out1, demultiplexer_3_out0, demultiplexer_3_out1,
       demultiplexer_4_out0, demultiplexer_4_out1, j_k_ff_2_qn, j_k_ff_3_qn, j_k_ff_4_qn, or_1_out;
  wire [3:0] not_1_out;

  and and_1 (and_1_out, j_k_ff_4_qn, j_k_ff_3_qn, j_k_ff_2_qn);
  and and_2 (and_2_out, O10D[3], j_k_ff_4_qn);
  and and_3 (and_3_out, j_k_ff_3_qn, j_k_ff_4_qn);
  and and_4 (and_4_out, O10D[2], j_k_ff_4_qn);
  and and_5 (and_5_out, O10D[3], j_k_ff_4_qn);
  or or_1 (or_1_out, and_4_out, and_5_out);
  J_K_Flip_Flop j_k_ff_1 (
    .J(and_1_out), .K(and_3_out), .clk(ENABLE), .Q(O10D[3]), .preset(demultiplexer_1_out0),
    .reset(demultiplexer_1_out1));  // open: Qn
  J_K_Flip_Flop j_k_ff_2 (
    .J(and_2_out), .K(and_3_out), .clk(ENABLE), .Q(O10D[2]), .Qn(j_k_ff_2_qn), .preset(demultiplexer_2_out0),
    .reset(demultiplexer_2_out1));
  J_K_Flip_Flop j_k_ff_3 (
    .J(or_1_out), .K(j_k_ff_4_qn), .clk(ENABLE), .Q(O10D[1]), .Qn(j_k_ff_3_qn),
    .preset(demultiplexer_3_out0), .reset(demultiplexer_3_out1));
  J_K_Flip_Flop j_k_ff_4 (
    .J(1'b1), .K(1'b1), .clk(ENABLE), .Q(O10D[0]), .Qn(j_k_ff_4_qn), .preset(demultiplexer_4_out0),
    .reset(demultiplexer_4_out1));
  Demultiplexer demultiplexer_1 (
    .out0(demultiplexer_1_out0), .out1(demultiplexer_1_out1), .in(ADD), .sel(not_1_out[3]));
  Demultiplexer demultiplexer_2 (
    .out0(demultiplexer_2_out0), .out1(demultiplexer_2_out1), .in(ADD), .sel(not_1_out[2]));
  Demultiplexer demultiplexer_3 (
    .out0(demultiplexer_3_out0), .out1(demultiplexer_3_out1), .in(ADD), .sel(not_1_out[1]));
  Demultiplexer demultiplexer_4 (
    .out0(demultiplexer_4_out0), .out1(demultiplexer_4_out1), .in(ADD), .sel(not_1_out[0]));
  assign not_1_out = ~SET;  // NOT_Gate not_1, 4 bits wide
  and and_6 (OVERFLOW, O10D[3], O10D[0]);
endmodule

module Modulo6down (
  input  ADD,
  input  [3:0] SET,
  input  ENABLE,
  output OVERFLOW,
  output [3:0] O6D
);

  wire and_1_out, and_2_out, demultiplexer_1_out0, demultiplexer_1_out1, demultiplexer_2_out0,
       demultiplexer_2_out1, demultiplexer_3_out0, demultiplexer_3_out1, JK0_qn, JK1_qn;
  wire [3:0] not_1_out;

  and and_1 (and_1_out, JK1_qn, JK0_qn);
  and and_2 (and_2_out, O6D[2], JK0_qn);
  J_K_Flip_Flop JK2 (
    .J(and_1_out), .K(JK0_qn), .clk(ENABLE), .Q(O6D[2]), .preset(demultiplexer_1_out0),
    .reset(demultiplexer_1_out1));  // open: Qn
  J_K_Flip_Flop JK1 (
    .J(and_2_out), .K(JK0_qn), .clk(ENABLE), .Q(O6D[1]), .Qn(JK1_qn), .preset(demultiplexer_2_out0),
    .reset(demultiplexer_2_out1));
  J_K_Flip_Flop JK0 (
    .J(1'b1), .K(1'b1), .clk(ENABLE), .Q(O6D[0]), .Qn(JK0_qn), .preset(demultiplexer_3_out0),
    .reset(demultiplexer_3_out1));
  Demultiplexer demultiplexer_1 (
    .out0(demultiplexer_1_out0), .out1(demultiplexer_1_out1), .in(ADD), .sel(not_1_out[2]));
  Demultiplexer demultiplexer_2 (
    .out0(demultiplexer_2_out0), .out1(demultiplexer_2_out1), .in(ADD), .sel(not_1_out[1]));
  Demultiplexer demultiplexer_3 (
    .out0(demultiplexer_3_out0), .out1(demultiplexer_3_out1), .in(ADD), .sel(not_1_out[0]));
  assign not_1_out = ~SET;  // NOT_Gate not_1, 4 bits wide
  and and_3 (OVERFLOW, O6D[2], O6D[0]);

  assign O6D[3] = 1'b0;
endmodule

module HoursCounter24 (
  input  HIGH,
  input  ENABLE,
  output [3:0] OM24U,
  output [3:0] OM24L
);

  wire and_1_out, modulo10counter_1_overflow;

  Modulo3Counter modulo3counter_1 (
    .HIGH(HIGH), .ENABLE(modulo10counter_1_overflow), .RESET(and_1_out), .OM3H(OM24U[1]), .OM3L(OM24U[0]));
  Modulo10Counter modulo10counter_1 (
    .HIGH(HIGH), .ENABLE(ENABLE), .RESET(and_1_out), .OVERFLOW(modulo10counter_1_overflow), .OM10(OM24L));
  and and_1 (and_1_out, OM24U[1], OM24L[2]);

  assign OM24U[3:2] = 2'b00;
endmodule

module HoursCounter12 (
  input  HIGH,
  input  ENABLE,
  input  RESET,
  input  SET12Hour,
  output [3:0] D10,
  output [3:0] D09,
  output [7:0] AMPM
);

  wire and_1_out, and_2_out, clock_1_out, d_ff_1_qn, for12_1_overflow, t_ff_1_q;

  Clock clock_1 (.out(clock_1_out));
  D_Flip_Flop d_ff_1 (.D(1'b1), .clk(clock_1_out), .Qn(d_ff_1_qn));  // open: Q, preset, reset
  For12 for12_1 (
    .HIGH(HIGH), .ENABLE(ENABLE), .RESET(d_ff_1_qn), .SET(and_1_out), .A(D09[3]), .B(D09[2]),
    .OVERFLOW(for12_1_overflow), .C(D09[1]), .D(D09[0]));
  and and_1 (and_1_out, D09[0], D09[1], D10[0]);
  and and_2 (and_2_out, D09[1], D10[0]);
  T_Flip_Flop t_ff_1 (.T(1'b1), .clk(and_2_out), .Q(t_ff_1_q), .preset(d_ff_1_qn));  // open: Qn, reset
  T_Flip_Flop #(.trigger("falling")) t_ff_2 (
    .T(1'b1), .clk(for12_1_overflow), .Q(D10[0]), .reset(and_1_out), .preset(d_ff_1_qn));  // open: Qn
  and and_3 (AMPM[6], t_ff_1_q, SET12Hour);

  assign {AMPM[7], AMPM[5:0]} = {2'b00, {5{SET12Hour}}};
  assign D10[3:1] = 3'b000;
endmodule

module For12 (
  input  HIGH,
  input  ENABLE,
  input  RESET,
  input  SET,
  output A,
  output B,
  output OVERFLOW,
  output C,
  output D
);

  wire or_1_out, or_2_out, or_3_out, or_4_out;

  T_Flip_Flop #(.trigger("falling")) t_ff_1 (.T(HIGH), .clk(B), .Q(A), .reset(or_1_out));  // open: Qn, preset
  T_Flip_Flop #(.trigger("falling")) t_ff_2 (.T(HIGH), .clk(C), .Q(B), .reset(or_2_out));  // open: Qn, preset
  T_Flip_Flop #(.trigger("falling")) t_ff_3 (.T(HIGH), .clk(D), .Q(C), .reset(or_3_out), .preset(RESET));  // open: Qn
  T_Flip_Flop #(.trigger("falling")) t_ff_4 (
    .T(HIGH), .clk(ENABLE), .Q(D), .reset(or_4_out), .preset(SET));  // open: Qn
  or or_1 (or_1_out, RESET, OVERFLOW, SET);
  or or_2 (or_2_out, RESET, OVERFLOW, SET);
  or or_3 (or_3_out, SET, OVERFLOW);
  or or_4 (or_4_out, RESET, OVERFLOW);
  and and_1 (OVERFLOW, A, C);
endmodule
